# Fritzing sketch bighead (saved by Fritzing 0.9.1b)
circuit board: 8.46667cm x 5.64444cm
breadboards: 1

parts:
  Parte1 = Arduino Nano (Rev3.0) (ICSP)
  VCC1 = Battery block 9V
  J3 = Basic Servo
  J4 = Basic Servo
  J5 = Basic Servo
  J6 = Basic Servo
  Parte2 = hc_sr04
  Q1 = NPN-Transistor [package="SOT-23 [SMD]"]
  R1 = Resistor [tolerance=±5% resistance=2.2k package=THT]
  D1 = Rectifier Diode [part_number=1N4001 package="300 mil [THT]"]

nets:
  GND: Parte1.GND, VCC1.-, J3.gnd, J4.gnd, J5.gnd, J6.gnd, Parte2.GND, Q1.2
  N1: Parte1.D3, Parte2.Echo
  N2: Parte1.D4, J6.pulse
  N3: Parte1.D5, J5.pulse
  N4: Parte1.D6, J4.pulse
  N5: Parte1.D7, J3.pulse
  N6: Parte1.D9, R1.Pin_0
  N7: Parte1.D12/MISO, Parte2.Trig
  N8: Parte1.VIN, VCC1.+
  VCC: Parte1.5V, J3.vcc, J4.vcc, J5.vcc, J6.vcc, Parte2.VCC
  N9: Q1.0, R1.Pin_1
  N10: Q1.1, D1.anode

// code stored in the sketch: bighead.ino
#include <Servo.h>
#include <PulseInOne.h>
#include "notas.h"

/** 
* On utilise des #define plutôt que des variables sur les constantes
* cela prend moins de place en mémoire vive !! (car remplacées lors de la complilation)
*/

#define BuzzerPin  9
int speakerPin = 9;
#define EnableServo 14  // activation des servos (la pin 14 est en faite la pin A0)

Servo Lleg;  // create servo object to control a servo 
Servo Rleg;
Servo Lfoot;
Servo Rfoot;

int Speed = 50;

int RFcenter = 90;    // variable to store the center servo position 
int LLcenter = 90;
int RLcenter = 87;
int LFcenter = 90;
int tAngle = 18; //tilt angle
int uAngle = 15; //turn angle
int sAngle = 30; //swing angle

long cm;                // variable pour stocker la distance de l'objet en cm

// Maximum distance we want to ping for (in centimeters). Maximum sensor distance is rated at 400-500cm.
#define MAX_DISTANCE 300
// Arduino pin tied to trigger pin on the ultrasonic sensor.
#define TRIGGER_PIN  12
// Arduino pin tied to echo pin on the ultrasonic sensor.
#define ECHO_PIN     2

//NewPing sonar(TRIGGER_PIN, ECHO_PIN, MAX_DISTANCE); // NewPing setup of pins and maximum distance.
int Obstacle = 0;

const float SpeedOfSound = 343.2; // ~speed of sound (m/s) in air, at 20°C         
const float MicrosecondsPerMillimetre = 1000.0 / SpeedOfSound; // microseconds per millimetre - sound travels 1 mm in ~2.9us
const float MicrosecondsToMillimetres = (1.0 / MicrosecondsPerMillimetre);
const float MicrosecondsToMillimetres2 = MicrosecondsToMillimetres / 2.0; // beam travels the distance twice... so halve the time.
unsigned long lastTime  = 0; 
int pingTimer     = 0;
int pingDelay     = 500; // milliseconds between ping pulses 
float millimetres     = 0.0;



/**
 * Arduino setup function
 * @return void
 */
void setup(){
  Lleg.attach(5);  // attaches the servo on pin x to the servo object 
  Rleg.attach(4);  // attaches the servo on pin x to the servo object 
  Lfoot.attach(7);  // attaches the servo on pin x to the servo object 
  Rfoot.attach(6);  // attaches the servo on pin x to the servo object 
  CenterServos(); //center the servos
  randomSeed(analogRead(0));
  //pinMode(green, OUTPUT);	digitalWrite(green, LOW);
  //pinMode(yellow, OUTPUT);	digitalWrite(yellow, LOW);
  //pinMode(red, OUTPUT);		digitalWrite(red, LOW);
  
  pinMode(BuzzerPin, OUTPUT);	digitalWrite(BuzzerPin, LOW);
  pinMode(BuzzerPin-1, OUTPUT);	digitalWrite(BuzzerPin-1, LOW); // branchement buzzer (identique a GND)
  //Buzzer.PlayMelody();
  
  Serial.begin(19200);
  Serial.println("Ready");


  pinMode(TRIGGER_PIN, OUTPUT);
  digitalWrite(TRIGGER_PIN, LOW);   
  PulseInOne::setup(pingPulseComplete);

  BuzzerBeep();
  for(int i=0;i<5;++i){
    delay(1000);
  }
  squeak();
}
void updatePingTimer(){
  unsigned long time = millis();
  unsigned long dt   = time - lastTime;
  lastTime       = time;
  
  pingTimer += dt;
  if(pingTimer > pingDelay){  
    pingTimer = 0;
    ping();
  }
}
void loop() { 
  Walk();
  /*switch (Obstacle){
    case 0: //no object
       Forward(10,90); //one step Forward
       BuzzerBeep();
       break;
     case 1: //object on Left
       TurnRight(2,60);
       BuzzerBeep();
       break;
     case 2: //object on Right
       TurnLeft(2,60);
       BuzzerBeep();
       break;
     case 3: //obect in Front (both Left and Right detect the object)
       TurnLeft(4,60); //turn around
       BuzzerBeep();
       break;
   }*/  
}


/**
 * Center servos
 */
void CenterServos() { 
    Lleg.write(LLcenter);
    // tell servo to go to position in variable 'center' 
    Rleg.write(RLcenter);
    // tell servo to go to position in variable 'center' 
    Lfoot.write(LFcenter);
    // tell servo to go to position in variable 'center' 
    Rfoot.write(RFcenter);
    // tell servo to go to position in variable 'center' 
    delay(100);
    // waits 100ms for the servos to reach the position 
}

void BuzzerBeep() {
	int tpstone=230;
	for (int i=0; i <= 999; i++) {
		digitalWrite(BuzzerPin, HIGH); delayMicroseconds(tpstone);
		digitalWrite(BuzzerPin, LOW); delayMicroseconds(tpstone);
	}
}

//La fonction ci-dessous fait clignoter la LED correspondant à la distance.
//Le clignotement est de plus en plus rapide à mesure que l'objet se rapproche.
void blink(int pause, int ledPin) {
  pause = pause * 10;
  digitalWrite(ledPin, HIGH);
  delay(pause);
  digitalWrite(ledPin, LOW);
  delay(10);
}

// code stored in the sketch: Radar.ino

/**
* Trigger the outward ping pulse(s)
*/
void ping(){ 
 // Serial.println("ping out");  
  digitalWrite(TRIGGER_PIN, HIGH);
  delayMicroseconds(10); // I think I can cope with blocking for a whole 10us here...
  digitalWrite(TRIGGER_PIN, LOW);
  
  // start listening out for the echo pulse on interrupt 0
  PulseInOne::begin();
}
 
 
/**
* Pulse complete callback hanlder for PulseInZero 
* @param duration - pulse length in microseconds
*/
void pingPulseComplete(unsigned long duration) { 
  millimetres = MicrosecondsToMillimetres2 * duration;
  if(millimetres < 200.00){
    Obstacle = random(1, 4);
  }
  if(millimetres > 4000){
    millimetres = 4000;
  } 
}

// code stored in the sketch: ServoPrimitives.ino
void TiltRightUp(byte ang, byte sp){    //tilt right up
  for (int i=0; i<=ang; i+=5){    Lfoot.write(LFcenter+i);    Rfoot.write(RFcenter+i);    delay(sp);  }
}
void TiltRightDown(byte ang, byte sp){  //tilt right down
  for (int i=ang; i>0; i-=5){    Lfoot.write(LFcenter+i);    Rfoot.write(RFcenter+i);    delay(sp);  }
}
void TiltLeftUp(byte ang, byte sp){  //tilt left up
  for (int i=0; i<=ang; i+=5){    Lfoot.write(LFcenter-i);    Rfoot.write(RFcenter-i);    delay(sp);  }
}
void TiltLeftDown(byte ang, byte sp){  //tilt left down
  for (int i=ang; i>0; i-=5){    Lfoot.write(LFcenter-i);    Rfoot.write(RFcenter-i);    delay(sp);  }
}

void LeftFootUp(char ang, byte sp){  //tilt left up
  for (int i=0; i<=ang; i+=5){    Lfoot.write(LFcenter-i);    delay(sp);  }
}
void LeftFootDown(byte ang, byte sp){  //tilt left down
  for (int i=ang; i>0; i-=5){    Lfoot.write(LFcenter-i);    delay(sp);  }
}
void RightFootUp(byte ang, byte sp){    //tilt right up
  for (int i=0; i<=ang; i+=5){    Rfoot.write(RFcenter+i);    delay(sp);  }
}
void RightFootDown(byte ang, byte sp){  //tilt right down
  for (int i=ang; i>0; i-=5){    Rfoot.write(RFcenter+i);    delay(sp);  }
}

void SwingRight(byte ang, byte sp){  //swing right
  for (int i=0; i<=ang; i+=5){    Lleg.write(LLcenter-i);    Rleg.write(RLcenter-i);    delay(sp);  }
}
void SwingRcenter(byte ang, byte sp){  //swing r->center
  for (int i=ang; i>0; i-=5){    Lleg.write(LLcenter-i);    Rleg.write(RLcenter-i);    delay(sp);  }
}

void SwingLeft(byte ang, byte sp){  //swing left
  for (byte i=0; i<=ang; i=i+5){    Lleg.write(LLcenter+i);    Rleg.write(RLcenter+i);    delay(sp);  }
}
void SwingLcenter(byte ang, byte sp){  //swing l->center
  for (byte i=ang; i>0; i=i-5){    Lleg.write(LLcenter+i);    Rleg.write(RLcenter+i);    delay(sp);  }
}

void RightLegIn(byte ang, byte sp){  //swing right
  for (int i=0; i<=ang; i+=5){    Rleg.write(RLcenter-i);    delay(sp);  }
}
void RightLegIcenter(byte ang, byte sp){  //swing r->center
  for (int i=ang; i>0; i-=5){    Rleg.write(RLcenter-i);    delay(sp);  }
}
void RightLegOut(byte ang, byte sp){  //swing right
  for (int i=0; i<=ang; i+=5){    Rleg.write(RLcenter+i);    delay(sp);  }
}
void RightLegOcenter(byte ang, byte sp){  //swing r->center
  for (int i=ang; i>0; i-=5){    Rleg.write(RLcenter+i);    delay(sp);  }
}
void LeftLegIn(byte ang, byte sp){  //swing left
  for (byte i=0; i<=ang; i=i+5){    Lleg.write(LLcenter+i);    delay(sp);  }
}
void LeftLegIcenter(byte ang, byte sp){  //swing l->center
  for (byte i=ang; i>0; i=i-5){    Lleg.write(LLcenter+i);    delay(sp);  }
}
void LeftLegOut(byte ang, byte sp){  //swing left
  for (byte i=0; i<=ang; i=i+5){    Lleg.write(LLcenter-i);    delay(sp);  }
}
void LeftLegOcenter(byte ang, byte sp){  //swing l->center
  for (byte i=ang; i>0; i=i-5){    Lleg.write(LLcenter-i);    delay(sp);  }
}

// code stored in the sketch: WalkFunctions.ino
void Walk(){
  Obstacle = 0;
  updatePingTimer();
  if(Obstacle==0)
    TiltRightUp(tAngle, Speed);
  while (Obstacle==0){
    stepForward(Speed);
    updatePingTimer();
  }
  TiltRightDown(tAngle, Speed);
  switch (Obstacle){
     case 1: //object on Left
        ohhh();
       TurnRight(2,60);
       break;
     case 2: //object on Right
        ohhh();
       TurnLeft(2,60);
       break;
     case 3: //obect in Front (both Left and Right detect the object)
        ohhh();
       TurnLeft(4,60); //turn around
       break;
   }
}

void stepForward(byte Speed){
  SwingRight(sAngle, Speed);
  TiltRightDown(tAngle, Speed);
  TiltLeftUp(tAngle, Speed);
  SwingRcenter(sAngle, Speed);
  SwingLeft(sAngle, Speed);
  TiltLeftDown(tAngle, Speed);
  TiltRightUp(tAngle, Speed);
  SwingLcenter(sAngle, Speed);
}

void stepBackward(byte Speed){
  RightLegIn(sAngle, Speed);
  TiltRightDown(uAngle, Speed);
  TiltLeftUp(uAngle, Speed);
  RightLegIcenter(sAngle, Speed);
  LeftLegOut(sAngle, Speed);
  TiltLeftDown(uAngle, Speed);
  TiltRightUp(uAngle, Speed);
  LeftLegOcenter(sAngle, Speed);
}

void TurnLeft(byte Steps, byte Speed){
  Back(1, Speed);
  TiltLeftUp(uAngle, Speed);
  delay(20);
  for (byte j=0; j<Steps; ++j){
    LeftLegIn(sAngle, Speed);
    TiltLeftDown(uAngle, Speed);
    TiltRightUp(uAngle, Speed);
    delay(20);
    LeftLegIcenter(sAngle, Speed);
    RightLegOut(sAngle, Speed);
    TiltRightDown(uAngle, Speed);
    TiltLeftUp(uAngle, Speed);
    delay(20);
    RightLegOcenter(sAngle, Speed);
  }
  TiltLeftDown(uAngle, Speed);  Obstacle = 0;
}

void TurnRight(byte Stps, byte Speed){
  Back(1, Speed);
  TiltRightUp(uAngle, Speed);
  delay(20);
  for (byte f=0; f<=Stps; ++f){
    RightLegIn(sAngle, Speed);
    TiltRightDown(uAngle, Speed);
    TiltLeftUp(uAngle, Speed);
    delay(20);
    RightLegIcenter(sAngle, Speed);
    LeftLegOut(sAngle, Speed);
    TiltLeftDown(uAngle, Speed);
    TiltRightUp(uAngle, Speed);
    delay(20);
    LeftLegOcenter(sAngle, Speed);
  }
  TiltRightDown(uAngle, Speed);Obstacle = 0;
}

void Back(byte Steps, byte Speed){
  digitalWrite(EnableServo,HIGH);
  TiltRightUp(uAngle, Speed);
  delay(20);
  for (byte j=0; j<Steps; ++j){
    RightLegIn(sAngle, Speed);
    TiltRightDown(uAngle, Speed);
    TiltLeftUp(uAngle, Speed);
    delay(20);
    RightLegIcenter(sAngle, Speed);
    LeftLegOut(sAngle, Speed);
    TiltLeftDown(uAngle, Speed);
    TiltRightUp(uAngle, Speed);
    delay(20);
    LeftLegOcenter(sAngle, Speed);
  }
  TiltRightDown(uAngle, Speed);
  digitalWrite(EnableServo,LOW);Obstacle = 0;
}
