# Fritzing sketch schema (saved by Fritzing 0.9.1b)

parts:
  J1 = Piezo Speaker
  VCC1 = Battery
  VCC2 = Battery
  Pied_droit = Basic Servo
  Corps_gauche = Basic Servo
  Corps_droit = Basic Servo
  Pied_gauche = Basic Servo
  Composants2 = hc_sr04
  LED1 = LED - 5mm [color="Red (633nm)" package="5 mm [THT]"]
  LED2 = LED - 5mm [color="Green (560nm)" package="5 mm [THT]"]
  LED3 = LED - 5mm [color="Yellow (595nm)" package="5 mm [THT]"]
  R1 = Resistor [tolerance=±5% resistance=10k package=THT]
  S1 = Toggle Switch [package=THT]
  R2 = Resistor [tolerance=±5% resistance=10k package=THT]
  R3 = Resistor [tolerance=±5% resistance=10k package=THT]
  IR1 = TSOP312.., 314.. [package=THT]
  Prog_arduino_(DTR_RX_TX_VCC_CTS_GND) = male pin header, 6 pins [form="♂ (male)"]
  C1 = Ceramic Capacitor [capacitance=0.1µF package="100 mil [THT, multilayer]"]
  Composants1 = Arduino Pro Mini v13

nets:
  GND: J1.pin1, VCC2.-, Pied_droit.gnd, Corps_gauche.gnd, Corps_droit.gnd, Pied_gauche.gnd, Composants2.GND, LED1.cathode, LED2.cathode, LED3.cathode, IR1.GND, Prog_arduino_(DTR_RX_TX_VCC_CTS_GND).pin1, Prog_arduino_(DTR_RX_TX_VCC_CTS_GND).pin2, Composants1.GND
  N1: J1.pin2, Composants1.D9_PWM
  N2: VCC1.-, VCC2.+
  N3: VCC1.+, S1.L2
  5V: Pied_droit.vcc, Corps_gauche.vcc, Corps_droit.vcc, Pied_gauche.vcc, Composants2.VCC, S1.L1, S1.COM, IR1.Vs, Prog_arduino_(DTR_RX_TX_VCC_CTS_GND).pin3, Composants1.VCC
  N4: Pied_droit.pulse, Composants1.D4
  N5: Corps_gauche.pulse, Composants1.D5_PWM
  N6: Corps_droit.pulse, Composants1.D6_PWM
  N7: Pied_gauche.pulse, Composants1.D7
  N8: Composants2.Trig, Composants1.D3_PWM
  N9: Composants2.Echo, Composants1.D2
  N10: LED1.anode, R1.Pin_1
  N11: LED2.anode, R3.Pin_1
  N12: LED3.anode, R2.Pin_1
  N13: R1.Pin_0, Composants1.D12/MISO
  N14: R2.Pin_0, Composants1.D11_PWM/MOSI
  N15: R3.Pin_0, Composants1.D10_PWM/SS
  N16: IR1.Data, Composants1.D13/SCK
  N17: Prog_arduino_(DTR_RX_TX_VCC_CTS_GND).pin4, Composants1.D1/RX
  N18: Prog_arduino_(DTR_RX_TX_VCC_CTS_GND).pin5, Composants1.D0/TX
  N19: Prog_arduino_(DTR_RX_TX_VCC_CTS_GND).pin6, C1.0
  N20: C1.1, Composants1.RESET
